// Logisim project logisim.circ as structural Verilog: 1 circuit, main circuit main
module main (
  input  IN0,
  input  IN1,
  input  IN2,
  output OUT2,
  output OUT1
);

  wire and_1_out, not_1_out, not_2_out;

  not not_1 (not_1_out, IN0);
  not not_2 (not_2_out, IN1);
  and and_1 (and_1_out, IN0, IN1, IN2);
  and and_2 (OUT1, not_1_out, not_2_out, IN2);
  or or_1 (OUT2, and_1_out, OUT1);
endmodule
